// Logisim project practice.circ as structural Verilog: 1 circuit, main circuit main
module main (
  input  A,
  input  B,
  input  C,
  input  D
);

  wire and_1_out, or_1_out;

  and and_1 (and_1_out, A, A, B);
  or or_1 (or_1_out, C, D);
  // AND_Gate and_2 has open pins: in0=and_1_out, in4=or_1_out, out=open
endmodule
